// Logisim project Somadores_Yasmin-Viegas.circ as structural Verilog: 5 circuits, main circuit meio_somador
module meio_somador (
  input  X,
  input  Y,
  output S,
  output Cout
);

  and and_1 (Cout, Y, X);
  xor xor_1 (S, X, Y);
endmodule

// Soma
module soma_completa (
  input  A,
  input  B,
  input  Cin,
  output S,
  output Cout
);

  wire and_1_out, and_2_out, xor_1_out;

  and and_1 (and_1_out, A, B);
  xor xor_1 (xor_1_out, A, B);
  xor xor_2 (S, xor_1_out, Cin);
  and and_2 (and_2_out, xor_1_out, Cin);
  or or_1 (Cout, and_2_out, and_1_out);
endmodule

// Somador
module somador_4_bits (
  input  A0,
  input  A1,
  input  A2,
  input  A3,
  input  Cin,
  input  B0,
  input  B0_2,
  input  B0_3,
  input  B0_4,
  output S0,
  output S0_2,
  output S0_3,
  output S0_4,
  output Cout,
  output Overflow
);

  wire soma_completa_1_cout, soma_completa_2_cout, soma_completa_3_cout;

  soma_completa soma_completa_1 (.Cin(Cin), .A(A0), .B(B0), .S(S0), .Cout(soma_completa_1_cout));
  soma_completa soma_completa_2 (.Cin(soma_completa_1_cout), .A(A1), .B(B0_2), .S(S0_2), .Cout(soma_completa_2_cout));
  soma_completa soma_completa_3 (.Cin(soma_completa_2_cout), .A(A2), .B(B0_3), .S(S0_3), .Cout(soma_completa_3_cout));
  soma_completa soma_completa_4 (.Cin(soma_completa_3_cout), .A(A3), .B(B0_4), .S(S0_4), .Cout(Cout));
  xor xor_1 (Overflow, soma_completa_3_cout, Cout);
endmodule

// decodificador
module decod (
  input  S0,
  input  S1,
  input  S2,
  input  S3,
  output a,
  output b,
  output c,
  output d,
  output e,
  output f,
  output g
);

  wire and_1_out, and_2_out, and_3_out, and_4_out, and_5_out, and_6_out, and_7_out, and_8_out, and_9_out,
       and_10_out, and_11_out, and_12_out, and_13_out, and_14_out, and_15_out, and_16_out, and_17_out,
       and_18_out, and_19_out, and_20_out, and_21_out, and_22_out, and_23_out, and_24_out, and_25_out,
       and_26_out, and_27_out, and_28_out, and_29_out, and_30_out, and_31_out, and_32_out, and_33_out,
       not_1_out, not_2_out, not_3_out, not_4_out, not_5_out, not_6_out, not_7_out, not_8_out, not_9_out,
       not_10_out, not_11_out, not_12_out, not_13_out, not_14_out, not_15_out, not_16_out, not_17_out,
       not_18_out, not_19_out, not_20_out, not_21_out, not_22_out, not_23_out, not_24_out, not_25_out,
       not_26_out, not_27_out, not_28_out, not_29_out, not_30_out, not_31_out, not_32_out, not_33_out,
       not_34_out, not_35_out, not_36_out, not_37_out, not_38_out, not_39_out, not_40_out, not_41_out,
       not_42_out;

  not not_1 (not_1_out, S1);
  and and_1 (and_1_out, not_1_out, not_2_out);
  not not_2 (not_2_out, S3);
  not not_3 (not_3_out, S0);
  and and_2 (and_2_out, not_3_out, S2);
  not not_4 (not_4_out, S0);
  and and_3 (and_3_out, not_4_out, S1, S3);
  and and_4 (and_4_out, S1, S2);
  and and_5 (and_5_out, S0, not_5_out, not_6_out);
  not not_5 (not_5_out, S1);
  not not_6 (not_6_out, S2);
  and and_6 (and_6_out, S0, not_7_out);
  not not_7 (not_7_out, S3);
  not not_8 (not_8_out, S0);
  and and_7 (and_7_out, not_8_out, not_9_out);
  not not_9 (not_9_out, S1);
  not not_10 (not_10_out, S0);
  and and_8 (and_8_out, not_10_out, not_11_out, not_12_out);
  not not_11 (not_11_out, S2);
  not not_12 (not_12_out, S3);
  not not_13 (not_13_out, S1);
  and and_9 (and_9_out, not_13_out, not_14_out);
  not not_14 (not_14_out, S3);
  not not_15 (not_15_out, S0);
  and and_10 (and_10_out, not_15_out, S2, S3);
  not not_16 (not_16_out, S2);
  and and_11 (and_11_out, S0, not_16_out, S3);
  not not_17 (not_17_out, S0);
  and and_12 (and_12_out, not_17_out, not_18_out);
  not not_18 (not_18_out, S2);
  not not_19 (not_19_out, S0);
  and and_13 (and_13_out, not_19_out, S3);
  not not_20 (not_20_out, S2);
  and and_14 (and_14_out, not_20_out, S3);
  not not_21 (not_21_out, S0);
  and and_15 (and_15_out, not_21_out, S1);
  and and_16 (and_16_out, S0, not_22_out);
  not not_22 (not_22_out, S1);
  not not_23 (not_23_out, S0);
  not not_24 (not_24_out, S1);
  and and_17 (and_17_out, not_23_out, not_24_out, not_25_out);
  not not_25 (not_25_out, S3);
  not not_26 (not_26_out, S1);
  and and_18 (and_18_out, not_26_out, S2, S3);
  not not_27 (not_27_out, S2);
  and and_19 (and_19_out, S1, not_27_out, S3);
  and and_20 (and_20_out, S1, S2, not_28_out);
  not not_28 (not_28_out, S3);
  not not_29 (not_29_out, S2);
  and and_21 (and_21_out, S0, not_29_out, not_30_out);
  not not_30 (not_30_out, S3);
  not not_31 (not_31_out, S1);
  and and_22 (and_22_out, not_31_out, not_32_out);
  not not_32 (not_32_out, S3);
  and and_23 (and_23_out, S2, not_33_out);
  not not_33 (not_33_out, S3);
  and and_24 (and_24_out, S0, S2);
  and and_25 (and_25_out, S0, S1, S3);
  not not_34 (not_34_out, S2);
  and and_26 (and_26_out, not_34_out, not_35_out);
  not not_35 (not_35_out, S3);
  not not_36 (not_36_out, S0);
  and and_27 (and_27_out, not_36_out, S1, not_37_out);
  not not_37 (not_37_out, S2);
  and and_28 (and_28_out, S1, not_38_out);
  not not_38 (not_38_out, S3);
  and and_29 (and_29_out, S0, not_39_out);
  not not_39 (not_39_out, S1);
  and and_30 (and_30_out, S0, S2);
  not not_40 (not_40_out, S1);
  and and_31 (and_31_out, not_40_out, S2);
  and and_32 (and_32_out, S1, not_41_out);
  not not_41 (not_41_out, S2);
  and and_33 (and_33_out, S1, not_42_out);
  not not_42 (not_42_out, S3);
  or or_1 (b, and_7_out, and_8_out, and_9_out, and_10_out, and_11_out);
  or or_2 (c, and_12_out, and_13_out, and_14_out, and_15_out, and_16_out);
  or or_3 (d, and_17_out, and_18_out, and_19_out, and_20_out, and_21_out);
  or or_4 (e, and_22_out, and_23_out, and_24_out, and_25_out);
  or or_5 (f, and_26_out, and_27_out, and_28_out, and_29_out, and_30_out);
  or or_6 (g, and_31_out, and_32_out, and_33_out, S0);
  or or_7 (a, and_1_out, and_2_out, and_3_out, and_4_out, and_5_out, and_6_out);
endmodule

module calculadora_4_bits (
  input  A0,
  input  A1,
  input  Cin,
  input  A2,
  input  A3,
  input  B0,
  input  B1,
  input  B2,
  input  B3,
  output S0,
  output S1,
  output Cout,
  output S2,
  output Overflow,
  output S3
);

  wire decod_1_a, decod_1_b, decod_1_c, decod_1_d, decod_1_e, decod_1_f, decod_1_g, decod_2_a, decod_2_b,
       decod_2_c, decod_2_d, decod_2_e, decod_2_f, decod_2_g, decod_3_a, decod_3_b, decod_3_c, decod_3_d,
       decod_3_e, decod_3_f, decod_3_g;

  decod decod_1 (
    .S0(A3), .S1(A2), .S2(A1), .S3(A0), .a(decod_1_a), .b(decod_1_b), .c(decod_1_c), .d(decod_1_d),
    .e(decod_1_e), .f(decod_1_f), .g(decod_1_g));
  somador_4_bits somador_4_bits_1 (
    .A0(A0), .A1(A1), .A2(A2), .A3(A3), .B0(B0), .B0_2(B1), .B0_3(B2), .B0_4(B3), .Cin(Cin), .Cout(Cout),
    .S0(S0), .S0_2(S1), .S0_3(S2), .S0_4(S3), .Overflow(Overflow));
  decod decod_2 (
    .S0(B3), .S1(B2), .S2(B1), .S3(B0), .a(decod_2_a), .b(decod_2_b), .c(decod_2_c), .d(decod_2_d),
    .e(decod_2_e), .f(decod_2_f), .g(decod_2_g));
  _7_Segment_Display u_7_segment_display_1 (
    .g(decod_1_g), .f(decod_1_f), .a(decod_1_a), .b(decod_1_b), .e(decod_1_e), .d(decod_1_d), .c(decod_1_c));  // open: dp
  _7_Segment_Display u_7_segment_display_2 (
    .g(decod_2_g), .f(decod_2_f), .a(decod_2_a), .b(decod_2_b), .e(decod_2_e), .d(decod_2_d), .c(decod_2_c));  // open: dp
  decod decod_3 (
    .S0(S3), .S1(S2), .S2(S1), .S3(S0), .a(decod_3_a), .b(decod_3_b), .c(decod_3_c), .d(decod_3_d),
    .e(decod_3_e), .f(decod_3_f), .g(decod_3_g));
  _7_Segment_Display u_7_segment_display_3 (
    .g(decod_3_g), .f(decod_3_f), .a(decod_3_a), .b(decod_3_b), .e(decod_3_e), .d(decod_3_d), .c(decod_3_c));  // open: dp
endmodule
