// Logisim project EP02-Parte1.circ as structural Verilog: 6 circuits, main circuit ULA_1bit
module ULA_1bit (
  input  Binvert,
  input  Cin,
  input  O1,
  input  O2,
  input  A,
  input  B,
  output S,
  output Cout
);

  wire and_1_out, mux_2bits_1_s, not_1_out, not_2_out, or_1_out, somador_completo_1_out_4;

  MUX_2bits mux_2bits_1 (.E0(B), .E1(not_1_out), .O1(Binvert), .S(mux_2bits_1_s));
  not not_1 (not_1_out, B);
  somador_completo somador_completo_1 (
    .in_2(A), .in_3(mux_2bits_1_s), .in_1(Cin), .out_5(Cout), .out_4(somador_completo_1_out_4));
  and and_1 (and_1_out, A, mux_2bits_1_s);
  or or_1 (or_1_out, A, mux_2bits_1_s);
  not not_2 (not_2_out, A);
  MUX_4bits mux_4bits_1 (
    .E0(and_1_out), .E1(or_1_out), .E2(not_2_out), .E3(somador_completo_1_out_4), .O1(O1), .O2(O2), .S(S));

  // Notes on the sheet:
  //   Yasmin Cassemiro Viegas - 800989
endmodule

module MUX_2bits (
  input  O1,
  input  E0,
  input  E1,
  output S
);

  wire and_1_out, and_2_out, not_1_out;

  not not_1 (not_1_out, O1);
  and and_1 (and_1_out, E0, not_1_out);
  and and_2 (and_2_out, E1, O1);
  or or_1 (S, and_1_out, and_2_out);
endmodule

module meio_somador (
  input  in_1,
  input  in_2,
  output out_3,
  output out_4
);

  xor xor_1 (out_3, in_1, in_2);
  and and_1 (out_4, in_2, in_1);
endmodule

module somador_completo (
  input  in_1,
  input  in_2,
  input  in_3,
  output out_4,
  output out_5
);

  wire meio_somador_1_out_3, meio_somador_1_out_4, meio_somador_2_out_4;

  meio_somador meio_somador_1 (.in_1(in_2), .in_2(in_3), .out_4(meio_somador_1_out_4), .out_3(meio_somador_1_out_3));
  meio_somador meio_somador_2 (.in_1(in_1), .in_2(meio_somador_1_out_3), .out_4(meio_somador_2_out_4), .out_3(out_4));
  or or_1 (out_5, meio_somador_2_out_4, meio_somador_1_out_4);
endmodule

module MUX_4bits (
  input  O1,
  input  O2,
  input  E0,
  input  E1,
  input  E2,
  input  E3,
  output S
);

  wire and_1_out, and_2_out, and_3_out, and_4_out, not_1_out, not_2_out, not_3_out, not_4_out;

  not not_1 (not_1_out, O1);
  not not_2 (not_2_out, O1);
  not not_3 (not_3_out, O2);
  not not_4 (not_4_out, O2);
  and and_1 (and_1_out, E0, not_1_out, not_3_out);
  and and_2 (and_2_out, E1, not_2_out, O2);
  and and_3 (and_3_out, E2, O1, not_4_out);
  and and_4 (and_4_out, E3, O1, O2);
  or or_1 (S, and_1_out, and_2_out, and_3_out, and_4_out);
endmodule

module ULA_4bit (
  input  A3,
  input  A2,
  input  A1,
  input  A0,
  input  B3,
  input  B2,
  input  B1,
  input  B0,
  input  Binvert,
  input  O2,
  input  O1,
  output S0,
  output S1,
  output S2,
  output S3,
  output out_16
);

  wire ula_1bit_1_cout, ula_1bit_2_cout, ula_1bit_3_cout;

  ULA_1bit ula_1bit_1 (
    .A(A0), .B(B0), .Binvert(Binvert), .Cin(Binvert), .O1(O2), .O2(O1), .Cout(ula_1bit_1_cout), .S(S0));
  ULA_1bit ula_1bit_2 (
    .A(A1), .B(B1), .Binvert(Binvert), .Cin(ula_1bit_1_cout), .O1(O2), .O2(O1), .Cout(ula_1bit_2_cout), .S(S1));
  ULA_1bit ula_1bit_3 (
    .A(A2), .B(B2), .Binvert(Binvert), .Cin(ula_1bit_2_cout), .O1(O2), .O2(O1), .Cout(ula_1bit_3_cout), .S(S2));
  ULA_1bit ula_1bit_4 (
    .A(A3), .B(B3), .Binvert(Binvert), .Cin(ula_1bit_3_cout), .O1(O2), .O2(O1), .Cout(out_16), .S(S3));

  // Notes on the sheet:
  //   Yasmin Cassemiro Viegas - 800989
endmodule
